// Logisim project 3bit_multiplier.circ as structural Verilog: 1 circuit, main circuit main
module main (
  input  a2,
  input  a1,
  input  a0,
  input  b0,
  input  b1,
  input  b2
);

  wire adder_1_cout, adder_1_out, adder_2_cout, adder_2_out, adder_3_cout, adder_3_out, adder_4_cout,
       adder_4_out, adder_5_cout, adder_5_out, adder_6_cout, adder_6_out, and_1_out, and_2_out, and_3_out,
       and_4_out, and_5_out, and_6_out, and_7_out, and_8_out, and_9_out;

  and and_1 (and_1_out, b0, a2);
  and and_2 (and_2_out, b1, a2);
  LED led_1 (.in(adder_6_cout));
  and and_3 (and_3_out, b2, a2);
  LED led_2 (.in(adder_6_out));
  and and_4 (and_4_out, b0, a1);
  and and_5 (and_5_out, b1, a1);
  and and_6 (and_6_out, b2, a1);
  LED led_3 (.in(adder_5_out));
  LED led_4 (.in(adder_4_out));
  and and_7 (and_7_out, b0, a0);
  LED led_5 (.in(adder_1_out));
  and and_8 (and_8_out, b1, a0);
  and and_9 (and_9_out, b2, a0);
  LED led_6 (.in(and_7_out));
  Adder #(.width(1)) adder_1 (.a(and_8_out), .b(and_4_out), .out(adder_1_out), .cin(1'b0), .cout(adder_1_cout));
  Adder #(.width(1)) adder_2 (.a(and_5_out), .b(and_1_out), .out(adder_2_out), .cin(adder_1_cout), .cout(adder_2_cout));
  Adder #(.width(1)) adder_3 (.a(and_2_out), .b(1'b0), .out(adder_3_out), .cin(adder_2_cout), .cout(adder_3_cout));
  Adder #(.width(1)) adder_4 (.a(adder_2_out), .b(and_9_out), .out(adder_4_out), .cin(1'b0), .cout(adder_4_cout));
  Adder #(.width(1)) adder_5 (
    .a(adder_3_out), .b(and_6_out), .out(adder_5_out), .cin(adder_4_cout), .cout(adder_5_cout));
  Adder #(.width(1)) adder_6 (
    .a(adder_3_cout), .b(and_3_out), .out(adder_6_out), .cin(adder_5_cout), .cout(adder_6_cout));

  // Notes on the sheet:
  //   wird von f13 berechnet!
  //   add21
  //   sum_for_22 ist das Problem
  //   add22
  //   add23
endmodule
